// Logisim project Equivalencias.circ as structural Verilog: 1 circuit, main circuit main
module main (
  input  in_1,
  input  in_2,
  input  A,
  input  B,
  input  A_2,
  input  B_2,
  output out_7,
  output out_8,
  output out_9
);

  wire and_1_out, and_2_out, and_3_out, not_1_out, not_2_out, not_3_out, not_4_out, not_5_out;

  not not_1 (not_1_out, in_1);
  not not_2 (not_2_out, in_2);
  not not_3 (not_3_out, A);
  not not_4 (not_4_out, A_2);
  not not_5 (not_5_out, B_2);
  or or_1 (out_8, not_3_out, B);
  and and_1 (and_1_out, not_1_out, not_2_out);
  not not_6 (out_7, and_1_out);
  and and_2 (and_2_out, A_2, B_2);
  and and_3 (and_3_out, not_4_out, not_5_out);
  or or_2 (out_9, and_2_out, and_3_out);

  // Notes on the sheet:
  //   Doble implicacion, A <-> B
  //   Equivalente a OR
  //   Equivalente a Implicacion Logica, A -> B
endmodule
