// Logisim project ClubTobi.circ as structural Verilog: 1 circuit, main circuit main
module main (
  input  Tobi,
  input  A,
  input  B,
  input  C,
  output out_5
);

  wire and_1_out, and_2_out, or_1_out;

  or or_1 (or_1_out, A, B, C);
  and and_1 (and_1_out, Tobi, or_1_out);
  and and_2 (and_2_out, A, B, C);
  or or_2 (out_5, and_1_out, and_2_out);

  // Notes on the sheet:
  //   El Club de Tobi
endmodule
